# Fritzing sketch DogBed_Fritz (saved by Fritzing 1.0.2b)
breadboards: 1

parts:
  A1 = Particle - Photon2
  Part1 = Thumb Joystick
  S1 = Pushbutton [package="[THT]"]
  Part2 = BME280 Breakout
  OLED_I2C1 = OLED 128x64 I2C Monochrome Display

nets:
  VCC: A1.Pin_2, A1.Pin_31, Part1.VCC, S1.Pin_3, Part2.3.3V, OLED_I2C1.VDD
  GND: A1.Pin_4, A1.Pin_15, A1.Pin_30, Part1.GND, S1.Pin_1, S1.Pin_2, Part2.GND, OLED_I2C1.GND
  N1: A1.Pin_6, Part1.HORZ
  N2: A1.Pin_7, Part1.VERT
  N3: A1.Pin_17, Part2.SDI/SDA, OLED_I2C1.SDA
  N4: A1.Pin_18, Part2.SCK/SCL, OLED_I2C1.SCK
  N5: A1.Pin_23, A1.Pin_37, Part1.SEL

notes:
  RE200B - Motion, Pyroelectric, PIR (Passive Infrared) Sensor Evaluation Board

custom parts:
  Particle - Photon2: The Photon 2 is a microcontroller and Wi-Fi networking developed by particle. Features: 802.11a/b/g/n Wi-Fi, 2.4 GHz and 5 GHz Integrated PCB antenna Integrated U.FL connector for external antenna Integrated RF switch BLE 5 using same antenna as Wi-Fi Realtek RTL8721DM MCU ARM Cortex M33 CPU, 200 MHz 2048 KB (2 MB) user application maximum size 3072 KB (3 MB) of RAM available to user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
  Pushbutton: A generic pushbutton.
